# Fritzing sketch tempLightSensor (saved by Fritzing 0.9.2b)
breadboards: 1

parts:
  Part2 = Arduino Ethernet Shield (Rev3)
  R1 = PHOTOCELL [package=photocell-kit]
  U1 = TMP36 [package=to-92-kit]
  C1 = Ceramic Capacitor [capacitance=100nF package="100 mil [THT, multilayer]"]
  R2 = Resistor [tolerance=±5% resistance=1k package=THT]

nets:
  3V3: Part2.AREF, Part2.3V3, R1.P$1, U1.VCC, C1.0
  N1: Part2.A0, U1.VOUT
  N2: Part2.A1, R1.P$2, R2.Pin_0, R2.Pin_1
  GND: Part2.GND, U1.GND, C1.1
